# Fritzing sketch udkPwm (saved by Fritzing 0.7.12b)
breadboards: 1

parts:
  U1 = atmega168 [package=dip]
  IC1 = ULN2803A [package=THT]
  C1 = Electrolytic Capacitor [capacitance=10µF part_number=10uF package="100 mil [THT, electrolytic]"]
  C3 = Ceramic Disk Capacitor [part_number=22pF package=THT]
  C4 = Ceramic Disk Capacitor [part_number=22pF package=THT]
  XTAL1 = Crystal [frequency="16 Mhz" part_number=16MHz package=THT]
  R1 = Resistor [tolerance=±5% resistance=150 part_number=150ohm package=THT]
  LED1 = LED - 5mm [color="Red (633nm)" package="5 mm [THT]"]
  R2 = Resistor [tolerance=±5% resistance=150 part_number=150ohm package=THT]
  LED2 = LED - 5mm [color="Red (633nm)" package="5 mm [THT]"]
  R3 = Resistor [tolerance=±5% resistance=150 part_number=150ohm package=THT]
  R4 = Resistor [tolerance=±5% resistance=150 part_number=150ohm package=THT]
  LED3 = LED - 5mm [color="Red (633nm)" package="5 mm [THT]"]
  LED4 = LED - 5mm [color="Red (633nm)" package="5 mm [THT]"]
  R5 = Resistor [tolerance=±5% resistance=150 part_number=150ohm package=THT]
  R6 = Resistor [tolerance=±5% resistance=150 part_number=150ohm package=THT]
  LED5 = LED - 5mm [color="Red (633nm)" package="5 mm [THT]"]
  LED6 = LED - 5mm [color="Red (633nm)" package="5 mm [THT]"]

nets:
  N1: U1.D3_(PWM), IC1.In_2
  5V: U1.VCC, IC1.COM_-_Common, C1.+, LED1.anode, LED2.anode, LED3.anode, LED4.anode, LED5.anode, LED6.anode
  GND: U1.GND#7, IC1.0V, C1.-, C3.pin_1, C4.pin_0
  N2: U1.XLAT1, C3.pin_0, XTAL1.pin_1
  N3: U1.XLAT2, C4.pin_1, XTAL1.pin_0
  N4: U1.D5_(PWM), IC1.In_1
  N5: U1.D6_(PWM), IC1.In_4
  N6: U1.D9_(PWM), IC1.In_3
  N7: U1.D10_(PWM), IC1.In_6
  N8: U1.D11_(PWM), IC1.In_5
  N9: IC1.Out_6, R6.Pin_1
  N10: IC1.Out_5, R5.Pin_1
  N11: IC1.Out_4, R3.Pin_1
  N12: IC1.Out_3, R4.Pin_1
  N13: IC1.Out_2, R2.Pin_1
  N14: IC1.Out_1, R1.Pin_1
  N15: R1.Pin_0, LED1.cathode
  N16: R2.Pin_0, LED2.cathode
  N17: R3.Pin_0, LED3.cathode
  N18: R4.Pin_0, LED4.cathode
  N19: R5.Pin_0, LED6.cathode
  N20: R6.Pin_0, LED5.cathode
