# Fritzing sketch ldr_schem (saved by Fritzing 0.7.12b)
breadboards: 1

parts:
  U1 = atmega168 [package=dip]
  R1 = Photocell (LDR) [package=THT]
  R2 = Resistor [tolerance=±5% resistance=10k part_number=10k package=THT]

nets:
  N1: U1.A0, R1.pin_1, R2.Pin_0
  5V: R1.pin_0
  GND: R2.Pin_1

notes:
  simplified schematics - missing power, chrystal and caps
