# Fritzing sketch speaker_schem (saved by Fritzing 0.7.12b)
breadboards: 1

parts:
  U1 = atmega168 [package=dip]
  R1 = Photocell (LDR) [part_number=ldr package=THT]
  R2 = Resistor [tolerance=±5% resistance=10k part_number=10k package=THT]
  SPKR1 = Loudspeaker [part_number=8ohm]
  R3 = Resistor [tolerance=±5% resistance=100 part_number=100ohm package=THT]
  XTAL1 = Crystal [part_number=16mhz package=THT]
  C1 = Ceramic Disk Capacitor [part_number=27pF package=THT]
  C2 = Ceramic Disk Capacitor [part_number=27pF package=THT]
  C3 = Electrolytic Capacitor [capacitance=10μF part_number=10uF package="0605 [SMD, electrolytic]"]
  IC1 = ULN2803A [package=THT]
  R4 = Resistor [tolerance=±5% resistance=150 part_number=150ohm package=THT]
  LED1 = LED - 5mm [color="Red (633nm)" package="5 mm [THT]"]

nets (from the schematic view):
  5V: U1.VCC, R1.pin_0, C3.+, IC1.COM_-_Common, LED1.anode
  GND: U1.GND#7, R2.Pin_1, SPKR1.pin2, C1.pin_0, C2.pin_0, C3.-, IC1.0V
  N1: U1.XLAT1, XTAL1.pin_0, C1.pin_1
  N2: U1.XLAT2, XTAL1.pin_1, C2.pin_1
  N3: U1.D5_(PWM), IC1.In_1
  N4: U1.D9_(PWM), R3.Pin_0
  N5: U1.A0, R1.pin_1, R2.Pin_0
  N6: SPKR1.pin1, R3.Pin_1
  N7: IC1.Out_1, R4.Pin_1
  N8: R4.Pin_0, LED1.cathode

custom parts:
  Ceramic Disk Capacitor: A 22 pF Ceramic Disk Capacitor
