# Fritzing sketch voltage_divider (saved by Fritzing 0.7.12b)
breadboards: 1

parts:
  R1 = Resistor [tolerance=±5% resistance=1k part_number=1K package=THT]
  R2 = Resistor [tolerance=±5% resistance=10k part_number=10K package=THT]
  R3 = Resistor [tolerance=±5% resistance=10k part_number=10K package=THT]
  R4 = Resistor [tolerance=±5% resistance=1k part_number=1K package=THT]
  R5 = Rotary Potentiometer (Large) [maximum_resistance=100kΩ package=THT]
  R6 = Photocell (LDR) [package=THT]
  R7 = Resistor [tolerance=±5% resistance=10k part_number=10K package=THT]

nets:
  5V: R1.Pin_0, R3.Pin_0, R5.leg1, R6.pin_0
  N1: R1.Pin_1, R2.Pin_0
  GND: R2.Pin_1, R4.Pin_1, R5.leg2, R7.Pin_1
  N2: R3.Pin_1, R4.Pin_0
  N3: R6.pin_1, R7.Pin_0

notes:
  one 1K resistor and then one 10K
  one 10K resistor and then one 1K
  one potentiometer with 3 legs
  one ldr with 2 legs - add resistor
