# Fritzing sketch electret_mic_power (saved by Fritzing 0.7.12b)
breadboards: 1

parts:
  R1 = Resistor [tolerance=±5% resistance=2.2k part_number=2.2K package=THT]
  C1 = Ceramic Capacitor [capacitance=100nF part_number=0.1uF package="100 mil [THT, multilayer]"]
  MIC1 = Microphone
  VCC1 = Battery
  TRS1 = Stereo Jack (TRS) 3.5mm [package="PG203J [THT]"]

nets:
  N1: R1.Pin_0, C1.1, MIC1.pin1
  N2: R1.Pin_1, VCC1.+
  N3: C1.0, TRS1.Ring
  N4: MIC1.pin2, VCC1.-, TRS1.Sleeve
