# Fritzing sketch lm386amp (saved by Fritzing 0.7.12b)
breadboards: 1

parts:
  IC1 = IC, DIP package, 8 pins [chip_label=IC]
  C1 = Electrolytic Capacitor [part_number=10uF package=THT]
  VCC1 = Battery block 9V
  SPKR1 = Loudspeaker [part_number=8ohm]
  C2 = Electrolytic Capacitor [part_number=220uF package=THT]
  R1 = Rotary Potentiometer (Small) [maximum_resistance=10kΩ part_number=10K]
  C3 = Electrolytic Capacitor [part_number=100uF package=THT]
  MIC1 = Microphone
  R2 = Resistor [tolerance=±5% resistance=2.2k part_number=2.2K package=THT]
  C4 = Ceramic Capacitor [capacitance=100nF part_number=100nF package="100 mil [THT, multilayer]"]

nets:
  N1: IC1.pin1, C1.+
  GND: IC1.pin2, IC1.pin4, VCC1.-, SPKR1.pin2, R1.leg1, C3.-
  N2: IC1.pin3, R1.wiper
  N3: IC1.pin5, C2.+
  9V: IC1.pin6, VCC1.+, C3.+, R2.Pin_0
  N4: IC1.pin8, C1.-
  N5: SPKR1.pin1, C2.-
  N6: R1.leg2, C4.0
  N7: MIC1.pin1, R2.Pin_1
  N8: MIC1.pin2, C4.1
